# Fritzing sketch PlanB (saved by Fritzing 1.0.1rc)
breadboards: 1

parts:
  AZ-Delivery_ESP32-WROOM-32 = MH-ET LIVE ESP32 DEVKIT 38 pins
  S1 = Pololu QTR-8 Reflectabce Sensor array [package=THT]
  DC_Motor_Driver = Adafruit DRV8833 DC/Stepper Motor Driver [part_number="Adafruit #3297"]
  M1 = DC Mini Metal Gear Motor
  M2 = DC Mini Metal Gear Motor
  IC1 = Voltage Regulator [package=to-220-alt]
  Battery_Pack_18650 = Battery

nets:
  N1: AZ-Delivery_ESP32-WROOM-32.3V3, S1.pin14, S1.pin22
  N2: AZ-Delivery_ESP32-WROOM-32.SVP, S1.pin4, S1.pin6
  N3: AZ-Delivery_ESP32-WROOM-32.SVN, S1.pin7
  N4: AZ-Delivery_ESP32-WROOM-32.IO34, S1.pin8
  N5: AZ-Delivery_ESP32-WROOM-32.IO35, S1.pin9
  N6: AZ-Delivery_ESP32-WROOM-32.IO32, S1.pin10
  N7: AZ-Delivery_ESP32-WROOM-32.IO33, S1.pin11
  N8: AZ-Delivery_ESP32-WROOM-32.5V, IC1.OUT
  N9: AZ-Delivery_ESP32-WROOM-32.IO19, DC_Motor_Driver.BIN2
  N10: AZ-Delivery_ESP32-WROOM-32.IO18, DC_Motor_Driver.BIN1
  N11: AZ-Delivery_ESP32-WROOM-32.IO17, DC_Motor_Driver.AIN2
  N12: AZ-Delivery_ESP32-WROOM-32.IO16, DC_Motor_Driver.AIN1
  GND: S1.pin1, S1.pin15, DC_Motor_Driver.GND, IC1.GND, Battery_Pack_18650.+
  N13: DC_Motor_Driver.AOUT2, M1.IN1
  N14: DC_Motor_Driver.AOUT1, M1.IN2
  N15: DC_Motor_Driver.BOUT1, M2.IN1
  N16: DC_Motor_Driver.BOUT2, M2.IN2
  N17: DC_Motor_Driver.VMOTOR, IC1.IN, Battery_Pack_18650.-

custom parts:
  MH-ET LIVE ESP32 DEVKIT 38 pins: http://mh.nodebb.com/topic/2/mh-et-live-esp32-devkit
  Adafruit DRV8833 DC/Stepper Motor Driver: Spin two DC motors or step one bi-polar or uni-polar stepper with up to 1.2A per channel using the DRV8833. This motor driver chip is a nice alternative to the TB6612 driver. Like that chip, you get 2 full H-bridges, but this chip is better for low voltage uses (can run from 2.7V up to 10.8V motor power) and has built in current limiting capability. We set it up for 1A current limiting so you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
  Battery: Your standard 2x 18650 battery pack (7.4 Volts)
